// Logisim project Single_Cycle_CPU.circ as structural Verilog: 1 circuit, main circuit Single_Cycle_CPU
module Single_Cycle_CPU (
);

  wire ALUSrc, and_1_out, and_2_out, BneOrBeq, Branch, clk, clock_1_out, Equal, ExpBlock, ExpSrc0, ExpSrc1,
       ExpSrc2, ExRegWrite, Halt, HasExp, immediate_extender_1_p7, instruction_statistics_1_p1,
       instruction_statistics_1_p2, instruction_statistics_1_p3, IsCOP0, IsEret, IsJAL, IsJR, IsShamt,
       IsSyscall, Jump, MemRead, MemtoReg, MemWrite, multiplexer_3_out, not_1_out, not_2_out, not_3_out,
       not_4_out, not_5_out, or_1_out, RegDst, RegWrite, xor_1_out, ZeroExtend;
  wire [3:0] ALUop, syscall_decoder_1_hex_2, syscall_decoder_1_hex_3, syscall_decoder_1_hex_4,
       syscall_decoder_1_hex_5;
  wire [4:0] multiplexer_6_out, multiplexer_7_out, regfile_1_p2, regfile_1_p3;
  wire [5:0] multiplexer_5_out;
  wire [8:0] demultiplexer_1_out0, demultiplexer_1_out1;
  wire [9:0] undriven_2;
  wire [15:0] syscall_decoder_1_hex;
  wire [25:0] multiplexer_5_out_2;
  wire [31:0] adder_1_out, adder_2_out, adder_3_out, bit_extender_1_out, counter_1_q, counter_2_q,
       counter_3_q, cp0_1_pcout, cycle_q, immediate_extender_1_p4, immediate_extender_1_p5,
       immediate_extender_1_p8, immediate_extender_1_p9, multiplexer_1_out, multiplexer_2_out,
       multiplexer_12_out, multiplexer_13_out, multiplexer_14_out, multiplexer_15_out, multiplexer_16_out,
       multiplexer_17_out, multiplexer_18_out, multiplexer_19_out, PC_Buffer_q, PC_q, ram_1_dout,
       regfile_1_p5, rom_1_data, rom_2_data, shifter_1_out, undriven;

  and and_1 (and_1_out, IsEret, IsCOP0);
  Multiplexer #(.width(32)) multiplexer_1 (
    .in0(32'h800), .in1(multiplexer_2_out), .out(multiplexer_1_out), .sel(not_1_out));
  Multiplexer #(.width(32)) multiplexer_2 (
    .in0(multiplexer_18_out), .in1(cp0_1_pcout), .out(multiplexer_2_out), .sel(and_1_out));
  not not_1 (not_1_out, HasExp);
  Clock clock_1 (.out(clock_1_out));
  Counter #(.max('hffffffff), .width(32)) cycle (.Q(cycle_q), .clk(clk));  // open: load, D, count, carry, up, clr
  // Probe on cycle_q
  Register #(.width(32)) PC (.D(multiplexer_1_out), .Q(PC_q), .clk(multiplexer_3_out));  // open: en, clr
  Multiplexer multiplexer_3 (.in0(clk), .in1(not_2_out), .out(multiplexer_3_out), .sel(or_1_out));
  or or_1 (or_1_out, HasExp, and_1_out);
  not not_2 (not_2_out, clk);
  Multiplexer multiplexer_4 (.in0(clock_1_out), .in1(1'b1), .out(clk), .sel(Halt));
  ROM #(.addrWidth(9), .dataWidth(32)) rom_1 (.addr(demultiplexer_1_out0), .data(rom_1_data));
  Demultiplexer #(.width(9)) demultiplexer_1 (
    .out0(demultiplexer_1_out0), .out1(demultiplexer_1_out1), .in(PC_q[10:2]), .sel(PC_q[11]));
  ROM #(.addrWidth(9), .dataWidth(32)) rom_2 (.addr(demultiplexer_1_out1), .data(rom_2_data));
  Adder #(.width(32)) adder_1 (.a(32'h4), .b(PC_q), .out(adder_1_out));  // open: cin, cout
  Counter #(.max('hffffffff), .width(32)) counter_1 (
    .count(instruction_statistics_1_p3), .Q(counter_1_q), .clk(clk));  // open: load, D, carry, up, clr
  // Probe on counter_1_q
  Counter #(.max('hffffffff), .width(32)) counter_2 (
    .count(instruction_statistics_1_p1), .Q(counter_2_q), .clk(clk));  // open: load, D, carry, up, clr
  Counter #(.max('hffffffff), .width(32)) counter_3 (
    .count(instruction_statistics_1_p2), .Q(counter_3_q), .clk(clk));  // open: load, D, carry, up, clr
  // Probe on counter_3_q
  Register #(.width(32)) PC_Buffer (.D(PC_q), .Q(PC_Buffer_q), .clk(HasExp));  // open: en, clr
  Adder #(.width(32)) adder_2 (.a(PC_q), .b(32'h4), .out(adder_2_out));  // open: cin, cout
  // Instruction_Statistics instruction_statistics_1: pin names not known; wires that end beside it: instruction_statistics_1_p1, instruction_statistics_1_p2, instruction_statistics_1_p3
  // Probe on counter_2_q
  Multiplexer #(.width(32)) multiplexer_5 (
    .in0(rom_1_data), .in1(rom_2_data), .out({multiplexer_5_out, multiplexer_5_out_2}), .sel(PC_q[11]));
  Multiplexer #(.width(5)) multiplexer_6 (
    .in0(multiplexer_5_out_2[20:16]), .in1(multiplexer_5_out_2[15:11]), .out(multiplexer_6_out), .sel(RegDst));
  Multiplexer #(.width(5)) multiplexer_7 (
    .in0(multiplexer_6_out), .in1({5{1'b1}}), .out(multiplexer_7_out), .sel(IsJAL));
  // Immediate_Extender immediate_extender_1: pin names not known; wires that end beside it: multiplexer_5_out_2[10:6], multiplexer_5_out_2[15:0], ZeroExtend, immediate_extender_1_p4, immediate_extender_1_p5, clk, immediate_extender_1_p7, immediate_extender_1_p8, immediate_extender_1_p9
  CP0 cp0_1 (
    .Inst({multiplexer_5_out, multiplexer_5_out_2}), .Expsrc0(ExpSrc0), .Expsrc1(ExpSrc1), .Expsrc2(ExpSrc2),
    .Din(immediate_extender_1_p9), .PCin(PC_Buffer_q), .clk(clk), .Enable(IsCOP0), .PCout(cp0_1_pcout),
    .Dout(immediate_extender_1_p5), .IsRet(IsEret), .ExRegWrite(ExRegWrite), .HasExp(HasExp),
    .ExpBlock(ExpBlock));
  // RegFile regfile_1: pin names not known; wires that end beside it: rom_1_data, regfile_1_p2, regfile_1_p3, multiplexer_7_out, regfile_1_p5
  Multiplexer #(.width(5)) multiplexer_8 (
    .in0(multiplexer_5_out_2[25:21]), .in1(5'b00010), .out(regfile_1_p2), .sel(IsSyscall));
  Multiplexer #(.width(5)) multiplexer_9 (
    .in0(multiplexer_5_out_2[20:16]), .in1(5'b00100), .out(regfile_1_p3), .sel(IsSyscall));
  not not_3 (not_3_out, IsJAL);
  Multiplexer multiplexer_10 (.in0(RegWrite), .in1(ExRegWrite), .out(immediate_extender_1_p7), .sel(IsCOP0));
  Multiplexer #(.width(32)) multiplexer_11 (
    .in0(immediate_extender_1_p5), .in1(multiplexer_12_out), .out(regfile_1_p5), .sel(not_4_out));
  not not_4 (not_4_out, IsCOP0);
  Multiplexer #(.width(32)) multiplexer_12 (
    .in0(adder_2_out), .in1(multiplexer_19_out), .out(multiplexer_12_out), .sel(not_3_out));
  Control control_1 (
    .op(multiplexer_5_out), .Funct(multiplexer_5_out_2[5:0]), .IsJAL(IsJAL), .IsShamt(IsShamt),
    .MemtoReg(MemtoReg), .RegWrite(RegWrite), .BneOrBeq(BneOrBeq), .ALUSrc(ALUSrc), .IsSyscall(IsSyscall),
    .ZeroExtend(ZeroExtend), .MemRead(MemRead), .MemWrite(MemWrite), .Jump(Jump), .Branch(Branch),
    .RegDst(RegDst), .IsJR(IsJR), .IsCOP0(IsCOP0), .ALUop(ALUop));  // open: ReadRs, ReadRt
  Syscall_Decoder syscall_decoder_1 (
    .v0(immediate_extender_1_p8), .a0(immediate_extender_1_p9), .clk(clk), .Enable(IsSyscall),
    .Hex({syscall_decoder_1_hex_5, syscall_decoder_1_hex_4, syscall_decoder_1_hex_3, syscall_decoder_1_hex_2, syscall_decoder_1_hex}),
    .Halt(Halt));
  assign bit_extender_1_out = {{27{1'b0}}, multiplexer_5_out_2[10:6]};  // Bit_Extender bit_extender_1
  Shifter #(.width(32)) shifter_1 (.in(immediate_extender_1_p4), .\dist (5'b00010), .out(shifter_1_out));
  xor xor_1 (xor_1_out, Equal, BneOrBeq);
  Multiplexer #(.width(32)) multiplexer_13 (
    .in0(immediate_extender_1_p8), .in1(immediate_extender_1_p9), .out(multiplexer_13_out), .sel(IsShamt));
  Multiplexer #(.width(32)) multiplexer_14 (
    .in0(immediate_extender_1_p9), .in1(immediate_extender_1_p4), .out(multiplexer_14_out), .sel(ALUSrc));
  Multiplexer #(.width(32)) multiplexer_15 (
    .in0(multiplexer_14_out), .in1(bit_extender_1_out), .out(multiplexer_15_out), .sel(IsShamt));
  Hex_Digit_Display hex_digit_display_1 (.value(syscall_decoder_1_hex_5));  // open: dp
  // alu alu_1: pin names not known; wires that end beside it: multiplexer_13_out, multiplexer_15_out, Equal, ALUop
  Adder #(.width(32)) adder_3 (.a(adder_1_out), .b(shifter_1_out), .out(adder_3_out));  // open: cin, cout
  and and_2 (and_2_out, Branch, xor_1_out);
  Hex_Digit_Display hex_digit_display_2 (.value(syscall_decoder_1_hex_4));  // open: dp
  Hex_Digit_Display hex_digit_display_3 (.value(syscall_decoder_1_hex_3));  // open: dp
  Multiplexer #(.width(32)) multiplexer_16 (
    .in0(adder_1_out), .in1(adder_3_out), .out(multiplexer_16_out), .sel(and_2_out));
  Hex_Digit_Display hex_digit_display_4 (.value(syscall_decoder_1_hex_2));  // open: dp
  Hex_Digit_Display hex_digit_display_5 (.value(syscall_decoder_1_hex[15:12]));  // open: dp
  RAM #(.addrWidth(10), .dataWidth(32)) ram_1 (
    .addr(undriven_2), .we(MemWrite), .oe(MemRead), .clk(clk), .din(immediate_extender_1_p9),
    .dout(ram_1_dout));
  Multiplexer #(.width(32)) multiplexer_17 (
    .in0({adder_1_out[31:28], multiplexer_5_out_2, 2'b00}), .in1(multiplexer_16_out),
    .out(multiplexer_17_out), .sel(not_5_out));
  not not_5 (not_5_out, Jump);
  Hex_Digit_Display hex_digit_display_6 (.value(syscall_decoder_1_hex[11:8]));  // open: dp
  Hex_Digit_Display hex_digit_display_7 (.value(syscall_decoder_1_hex[7:4]));  // open: dp
  Hex_Digit_Display hex_digit_display_8 (.value(syscall_decoder_1_hex[3:0]));  // open: dp
  Button button_1 (.out(ExpSrc0));
  Multiplexer #(.width(32)) multiplexer_18 (
    .in0(multiplexer_17_out), .in1(immediate_extender_1_p8), .out(multiplexer_18_out), .sel(IsJR));
  Button button_2 (.out(ExpSrc1));
  Multiplexer #(.width(32)) multiplexer_19 (
    .in0({undriven[31:12], undriven_2, undriven[1:0]}), .in1(ram_1_dout), .out(multiplexer_19_out),
    .sel(MemtoReg));
  Button button_3 (.out(ExpSrc2));

  // Notes on the sheet:
  //   Screen
endmodule
